# Fritzing sketch AirMouseDesign2 (saved by Fritzing 0.9.3b)
breadboards: 1

parts:
  S1 = Pushbutton [package="[THT]"]
  S2 = Pushbutton [package="[THT]"]
  Part1 = Arduino Leonardo (Rev3b)
  R2 = Resistor [tolerance=±5% resistance=220 package="2010 [SMD]"]
  Part3 = Triple Axis Gyro Breakout ITG-3200
  R3 = Resistor [tolerance=±5% resistance=220 package="1206 [SMD]"]

nets:
  N1: S1.Pin_1, S1.Pin_2, Part1.D4/A6, R2.Pin_0
  N2: S1.Pin_3, S1.Pin_4, S2.Pin_3, S2.Pin_4, Part1.3V3
  N3: S2.Pin_1, S2.Pin_2, Part1.D5_PWM, R3.Pin_0
  N4: Part1.D2/SDA, Part3.SDA
  N5: Part1.D3_PWM/SCL, Part3.SCL
  5V: Part1.5V, Part3.VCC
  GND: Part1.GND, R2.Pin_1, Part3.GND, R3.Pin_1
